// Logisim project cpu.circ as structural Verilog: 2 circuits, main circuit main
module main (
  input  [31:0] INSTRUCTION,
  input  CLOCK,
  output [31:0] FETCH_ADDRESS,
  output [31:0] s0_Value,
  output [31:0] s1_Value,
  output [31:0] s2_Value,
  output [31:0] ra_Value,
  output [31:0] sp_Value
);

  wire ALUSrc, eql, ExtOp, jal, lui, main_2_signed_overflow, MemToReg, MemWr, op0, RegWr, shift, xor_1_out;
  wire [1:0] nPCsel, RegDst;
  wire [3:0] ALUCtr;
  wire [4:0] multiplexer_1_out, multiplexer_2_out;
  wire [31:0] adder_2_out, bit_extender_2_out, immed, main_2_result, main_3_p5, multiplexer_3_out,
       multiplexer_4_out, multiplexer_5_out, multiplexer_6_out, multiplexer_7_out, multiplexer_8_out, PC_4,
       R_rs, rt, shifter_1_out, shifter_2_out, shifter_3_out, WrtData;

  Adder #(.width(32)) adder_1 (.a(INSTRUCTION), .b(32'h4), .out(PC_4));  // open: cin, cout
  Multiplexer #(.select(2), .width(5), .enable("false")) multiplexer_1 (
    .in0(INSTRUCTION[20:16]), .in1(INSTRUCTION[15:11]), .in2(INSTRUCTION[25:21]), .out(multiplexer_1_out),
    .sel(RegDst));  // open: in3
  assign immed = {{16{ExtOp}}, INSTRUCTION[15:0]};  // Bit_Extender bit_extender_1
  Multiplexer #(.width(5), .enable("false")) multiplexer_2 (
    .in0(multiplexer_1_out), .in1({5{1'b1}}), .out(multiplexer_2_out), .sel(jal));
  Shifter #(.width(32)) shifter_1 (.in(immed), .\dist (5'b00010), .out(shifter_1_out));
  Shifter #(.width(32)) shifter_2 (.in(INSTRUCTION), .\dist (5'b00010), .out(shifter_2_out));
  Adder #(.width(32)) adder_2 (.a(PC_4), .b(shifter_1_out), .out(adder_2_out));  // open: cin, cout
  xor xor_1 (xor_1_out, eql, op0);
  regfile_main main_1 (
    .Read_Register_1(INSTRUCTION[25:21]), .Read_Register_2(INSTRUCTION[20:16]),
    .Write_Register(multiplexer_2_out), .Write_Data(WrtData), .Write_Enable(RegWr), .Clock(CLOCK),
    .Read_Data_1(R_rs), .Read_Data_2(rt), .s0_Value(s0_Value), .s1_Value(s1_Value), .s2_Value(s2_Value),
    .ra_Value(ra_Value), .sp_Value(sp_Value));
  Multiplexer #(.width(32), .enable("false")) multiplexer_3 (
    .in0(PC_4), .in1(adder_2_out), .out(multiplexer_3_out), .sel(xor_1_out));
  Multiplexer #(.width(32), .enable("false")) multiplexer_4 (
    .in0(rt), .in1(immed), .out(multiplexer_4_out), .sel(ALUSrc));
  Multiplexer #(.select(2), .width(32), .enable("false")) multiplexer_5 (
    .in0(PC_4), .in1(multiplexer_3_out), .in2({PC_4[31:28], shifter_2_out[27:0]}), .in3(R_rs),
    .out(multiplexer_5_out), .sel(nPCsel));
  Register #(.width(32)) PC (.D(multiplexer_5_out), .Q(FETCH_ADDRESS), .clk(CLOCK));  // open: en, clr
  assign bit_extender_2_out = {{27{1'b0}}, INSTRUCTION[10:6]};  // Bit_Extender bit_extender_2
  Multiplexer #(.width(32), .enable("false")) multiplexer_6 (
    .in0(R_rs), .in1(bit_extender_2_out), .out(multiplexer_6_out), .sel(shift));
  LED led_1 (.in(main_2_signed_overflow));
  alu_main main_2 (
    .Switch(ALUCtr), .X(multiplexer_6_out), .Equal(eql), .Result(main_2_result),
    .Signed_Overflow(main_2_signed_overflow), .Y(multiplexer_4_out));
  Shifter #(.width(32)) shifter_3 (.in(immed), .\dist (5'b10000), .out(shifter_3_out));
  Multiplexer #(.width(32), .enable("false")) multiplexer_7 (
    .in0(main_2_result), .in1(shifter_3_out), .out(multiplexer_7_out), .sel(lui));
  // mem_main main_3: pin names not known; wires that end beside it: multiplexer_7_out, rt, MemWr, CLOCK, main_3_p5
  Multiplexer #(.width(32), .enable("false")) multiplexer_8 (
    .in0(multiplexer_7_out), .in1(main_3_p5), .out(multiplexer_8_out), .sel(MemToReg));
  Multiplexer #(.width(32), .enable("false")) multiplexer_9 (
    .in0(multiplexer_8_out), .in1(PC_4), .out(WrtData), .sel(jal));

  // Other names for the same wires on the sheet: clk = CLOCK; fetch_addr[31:0] = FETCH_ADDRESS;
  //   funct[5:0] = INSTRUCTION[5:0]; shamt[4:0] = INSTRUCTION[10:6]; opcode[5:0] = INSTRUCTION[31:26];
  //   ra[31:0] = ra_Value; s0[31:0] = s0_Value; s1[31:0] = s1_Value; s2[31:0] = s2_Value; sp[31:0] = sp_Value

  // Notes on the sheet:
  //   Output
  //   These are outputs/inputs from run.circ
  //   Inputs
  //   These are DEBUG/TEST outputs from your circuit.
endmodule

module ctrSignals (
  input  [5:0] opcode,
  input  [5:0] funct,
  output ALUSrc,
  output RegWr,
  output [1:0] RegDst,
  output MemToReg,
  output MemWr,
  output [1:0] nPCsel,
  output shift,
  output jal,
  output lui,
  output ExtOp
);

  wire add, addi, addiu, addu, \and , andi, beq, bne, j, jal_t, jr, lui_t, lw, \or , ori, rtype, sll, slt,
       slti, sltiu, sltu, sra, srl, sub, subu, sw, swinc;

  and and_1 (rtype, ~opcode[0], ~opcode[1], ~opcode[2], ~opcode[3], ~opcode[4], ~opcode[5]);  // AND_Gate
  and and_2 (add, ~funct[1], ~funct[1], ~funct[2], ~funct[3], ~funct[4], funct[5], rtype);  // AND_Gate
  and and_3 (addu, funct[1], ~funct[1], ~funct[2], ~funct[3], ~funct[4], funct[5], rtype);  // AND_Gate
  and and_4 (\and , ~funct[1], ~funct[1], funct[2], ~funct[3], ~funct[4], funct[5], rtype);  // AND_Gate
  and and_5 (jr, ~funct[1], ~funct[1], ~funct[2], funct[3], ~funct[4], ~funct[5], rtype);  // AND_Gate
  and and_6 (\or , funct[1], ~funct[1], funct[2], ~funct[3], ~funct[4], funct[5], rtype);  // AND_Gate
  and and_7 (slt, ~funct[1], funct[1], ~funct[2], funct[3], ~funct[4], funct[5], rtype);  // AND_Gate
  and and_8 (sltu, funct[1], funct[1], ~funct[2], funct[3], ~funct[4], funct[5], rtype);  // AND_Gate
  and and_9 (sll, ~funct[1], ~funct[1], ~funct[2], ~funct[3], ~funct[4], ~funct[5], rtype);  // AND_Gate
  and and_10 (sra, funct[1], ~funct[1], ~funct[2], funct[3], funct[4], ~funct[5], rtype);  // AND_Gate
  and and_11 (srl, ~funct[1], funct[1], ~funct[2], ~funct[3], ~funct[4], ~funct[5], rtype);  // AND_Gate
  and and_12 (sub, ~funct[1], funct[1], ~funct[2], ~funct[3], ~funct[4], funct[5], rtype);  // AND_Gate
  and and_13 (subu, funct[1], funct[1], ~funct[2], ~funct[3], ~funct[4], funct[5], rtype);  // AND_Gate
  and and_14 (addi, ~opcode[0], ~opcode[1], ~opcode[2], opcode[3], ~opcode[4], ~opcode[5]);  // AND_Gate
  and and_15 (addiu, opcode[0], ~opcode[1], ~opcode[2], opcode[3], ~opcode[4], ~opcode[5]);  // AND_Gate
  and and_16 (andi, ~opcode[0], ~opcode[1], opcode[2], opcode[3], ~opcode[4], ~opcode[5]);  // AND_Gate
  and and_17 (beq, ~opcode[0], ~opcode[1], opcode[2], ~opcode[3], ~opcode[4], ~opcode[5]);  // AND_Gate
  and and_18 (bne, opcode[0], ~opcode[1], opcode[2], ~opcode[3], ~opcode[4], ~opcode[5]);  // AND_Gate
  and and_19 (j, ~opcode[0], opcode[1], ~opcode[2], ~opcode[3], ~opcode[4], ~opcode[5]);  // AND_Gate
  and and_20 (jal_t, opcode[0], opcode[1], ~opcode[2], ~opcode[3], ~opcode[4], ~opcode[5]);  // AND_Gate
  and and_21 (lui_t, opcode[0], opcode[1], opcode[2], opcode[3], opcode[4], opcode[5]);
  and and_22 (lw, opcode[0], opcode[1], ~opcode[2], ~opcode[3], ~opcode[4], opcode[5]);  // AND_Gate
  and and_23 (ori, opcode[0], ~opcode[1], opcode[2], opcode[3], ~opcode[4], ~opcode[5]);  // AND_Gate
  and and_24 (slti, ~opcode[0], opcode[1], ~opcode[2], opcode[3], ~opcode[4], ~opcode[5]);  // AND_Gate
  and and_25 (sltiu, opcode[0], opcode[1], ~opcode[2], opcode[3], ~opcode[4], ~opcode[5]);  // AND_Gate
  and and_26 (sw, opcode[0], opcode[1], ~opcode[2], opcode[3], ~opcode[4], opcode[5]);  // AND_Gate
  and and_27 (swinc, ~opcode[0], ~opcode[1], opcode[2], opcode[3], ~opcode[4], opcode[5]);  // AND_Gate

  assign funct[0] = funct[1];

  // Other names for the same wires on the sheet: fn0 = funct[1]; fn1 = funct[1]; fn2 = funct[2]; fn3 = funct[3];
  //   fn4 = funct[4]; fn5 = funct[5]; op0 = opcode[0]; op1 = opcode[1]; op2 = opcode[2]; op3 = opcode[3];
  //   op4 = opcode[4]; op5 = opcode[5]
endmodule
