// Logisim project regfile.circ as structural Verilog: 1 circuit, main circuit main
module main (
  input  [4:0] Read_Register_1,
  input  [4:0] Read_Register_2,
  input  [4:0] Write_Register,
  input  [31:0] Write_Data,
  input  Write_Enable,
  input  Clock,
  output [31:0] s0_Value,
  output [31:0] s1_Value,
  output [31:0] s2_Value,
  output [31:0] ra_Value,
  output [31:0] sp_Value,
  output [31:0] Read_Data_1,
  output [31:0] Read_Data_2
);

  wire in01, in02, in03, in04, in05, in06, in07, in08, in09, in10, in11, in12, in13, in14, in15, in16, in17,
       in18, in19, in20, in21, in22, in23, in24, in25, in26, in27, in28, in29, in30, in31;
  wire [31:0] _1, _2, _3, _4, _5, _6, _7, _8, _9, _10, _11, _12, _13, _14, _15, _19, _20, _21, _22, _23, _24,
       _25, _26, _27, _28, _30;

  Register #(.width(32)) register_1 (.D(Write_Data), .en(in04), .Q(_4), .clk(Clock));  // open: clr
  Register #(.width(32)) register_2 (.D(Write_Data), .en(in08), .Q(_8), .clk(Clock));  // open: clr
  Register #(.width(32)) register_3 (.D(Write_Data), .en(in12), .Q(_12), .clk(Clock));  // open: clr
  Register #(.width(32)) register_4 (.D(Write_Data), .en(in16), .Q(s0_Value), .clk(Clock));  // open: clr
  Register #(.width(32)) register_5 (.D(Write_Data), .en(in20), .Q(_20), .clk(Clock));  // open: clr
  Register #(.width(32)) register_6 (.D(Write_Data), .en(in24), .Q(_24), .clk(Clock));  // open: clr
  Register #(.width(32)) register_7 (.D(Write_Data), .en(in28), .Q(_28), .clk(Clock));  // open: clr
  Multiplexer #(.select(5), .width(32), .enable("false")) multiplexer_1 (
    .in0({32{1'b0}}), .in1(_1), .in2(_2), .in3(_3), .in4(_4), .in5(_5), .in6(_6), .in7(_7), .in8(_8),
    .in9(_9), .in10(_10), .in11(_11), .in12(_12), .in13(_13), .in14(_14), .in15(_15), .in16(s0_Value),
    .in17(s1_Value), .in18(s2_Value), .in19(_19), .in20(_20), .in21(_21), .in22(_22), .in23(_23), .in24(_24),
    .in25(_25), .in26(_26), .in27(_27), .in28(_28), .in29(sp_Value), .in30(_30), .in31(ra_Value),
    .out(Read_Data_2), .sel(Read_Register_2));
  Multiplexer #(.select(5), .width(32), .enable("false")) multiplexer_2 (
    .in0({32{1'b0}}), .in1(_1), .in2(_2), .in3(_3), .in4(_4), .in5(_5), .in6(_6), .in7(_7), .in8(_8),
    .in9(_9), .in10(_10), .in11(_11), .in12(_12), .in13(_13), .in14(_14), .in15(_15), .in16(s0_Value),
    .in17(s1_Value), .in18(s2_Value), .in19(_19), .in20(_20), .in21(_21), .in22(_22), .in23(_23), .in24(_24),
    .in25(_25), .in26(_26), .in27(_27), .in28(_28), .in29(sp_Value), .in30(_30), .in31(ra_Value),
    .out(Read_Data_1), .sel(Read_Register_1));
  Register #(.width(32)) register_8 (.D(Write_Data), .en(in01), .Q(_1), .clk(Clock));  // open: clr
  Register #(.width(32)) register_9 (.D(Write_Data), .en(in05), .Q(_5), .clk(Clock));  // open: clr
  Register #(.width(32)) register_10 (.D(Write_Data), .en(in09), .Q(_9), .clk(Clock));  // open: clr
  Register #(.width(32)) register_11 (.D(Write_Data), .en(in13), .Q(_13), .clk(Clock));  // open: clr
  Register #(.width(32)) register_12 (.D(Write_Data), .en(in17), .Q(s1_Value), .clk(Clock));  // open: clr
  Register #(.width(32)) register_13 (.D(Write_Data), .en(in21), .Q(_21), .clk(Clock));  // open: clr
  Register #(.width(32)) register_14 (.D(Write_Data), .en(in25), .Q(_25), .clk(Clock));  // open: clr
  Register #(.width(32)) register_15 (.D(Write_Data), .en(in29), .Q(sp_Value), .clk(Clock));  // open: clr
  Register #(.width(32)) register_16 (.D(Write_Data), .en(in02), .Q(_2), .clk(Clock));  // open: clr
  Register #(.width(32)) register_17 (.D(Write_Data), .en(in06), .Q(_6), .clk(Clock));  // open: clr
  Register #(.width(32)) register_18 (.D(Write_Data), .en(in10), .Q(_10), .clk(Clock));  // open: clr
  Register #(.width(32)) register_19 (.D(Write_Data), .en(in14), .Q(_14), .clk(Clock));  // open: clr
  Register #(.width(32)) register_20 (.D(Write_Data), .en(in18), .Q(s2_Value), .clk(Clock));  // open: clr
  Register #(.width(32)) register_21 (.D(Write_Data), .en(in22), .Q(_22), .clk(Clock));  // open: clr
  Register #(.width(32)) register_22 (.D(Write_Data), .en(in26), .Q(_26), .clk(Clock));  // open: clr
  Register #(.width(32)) register_23 (.D(Write_Data), .en(in30), .Q(_30), .clk(Clock));  // open: clr
  Register #(.width(32)) register_24 (.D(Write_Data), .en(in03), .Q(_3), .clk(Clock));  // open: clr
  Register #(.width(32)) register_25 (.D(Write_Data), .en(in07), .Q(_7), .clk(Clock));  // open: clr
  Register #(.width(32)) register_26 (.D(Write_Data), .en(in11), .Q(_11), .clk(Clock));  // open: clr
  Register #(.width(32)) register_27 (.D(Write_Data), .en(in15), .Q(_15), .clk(Clock));  // open: clr
  Register #(.width(32)) register_28 (.D(Write_Data), .en(in19), .Q(_19), .clk(Clock));  // open: clr
  Register #(.width(32)) register_29 (.D(Write_Data), .en(in23), .Q(_23), .clk(Clock));  // open: clr
  Register #(.width(32)) register_30 (.D(Write_Data), .en(in27), .Q(_27), .clk(Clock));  // open: clr
  Register #(.width(32)) register_31 (.D(Write_Data), .en(in31), .Q(ra_Value), .clk(Clock));  // open: clr
  Demultiplexer #(.select(5), .disabled(0), .enable("false")) demultiplexer_1 (
    .out1(in01), .out2(in02), .out3(in03), .out4(in04), .out5(in05), .out6(in06), .out7(in07), .out8(in08),
    .out9(in09), .out10(in10), .out11(in11), .out12(in12), .out13(in13), .out14(in14), .out15(in15),
    .out16(in16), .out17(in17), .out18(in18), .out19(in19), .out20(in20), .out21(in21), .out22(in22),
    .out23(in23), .out24(in24), .out25(in25), .out26(in26), .out27(in27), .out28(in28), .out29(in29),
    .out30(in30), .out31(in31), .in(Write_Enable), .sel(Write_Register));  // open: out0

  // Other names for the same wires on the sheet: _16[31:0] = s0_Value; _17[31:0] = s1_Value; _18[31:0] = s2_Value;
  //   _29[31:0] = sp_Value; _31[31:0] = ra_Value; clk = Clock; read_data1[31:0] = Read_Data_1;
  //   read_data2[31:0] = Read_Data_2; read_reg1[4:0] = Read_Register_1; read_reg2[4:0] = Read_Register_2;
  //   write_en = Write_Enable; write_reg[4:0] = Write_Register

  // Notes on the sheet:
  //   INPUTS to your circuit
  //   DON'T CHANGE THE LOCATIONS OF THE INPUTS AND OUTPUTS!
  //   These are DEBUG/TEST outputs from your circuit.
  //   OUTPUTS from your circuit
endmodule
